# Fritzing sketch irsensor_schema (saved by Fritzing 1.0.6)
breadboards: 1
perfboards: 1

parts:
  Composant1 = Arduino Uno (Rev3) - ICSP
  Raspberry_Pi_1 = Raspberry Pi 3 [part_number=RPI-3-V1.2]
  R1 = PHOTOCELL [package=photocell]
  R2 = PHOTOCELL [package=photocell]
  R5 = Resistor [tolerance=±5% power=0.25W resistance=3000 package=THT]
  R6 = Resistor [tolerance=±5% power=0.25W resistance=3000 package=THT]
  R7 = Resistor [tolerance=±5% power=0.25W resistance=1000 package=THT]
  R8 = Resistor [tolerance=±5% power=0.25W resistance=220 package=THT]
  LED1 = LED - 5mm [color="Infrared (940nm)" current=0.030A package="5 mm [THT]"]
  LED2 = LED - 5mm [color="Infrared (940nm)" current=0.030A package="5 mm [THT]"]
  R9 = Resistor [tolerance=±5% power=0.25W resistance=220 package=THT]
  R10 = Resistor [tolerance=±5% power=0.25W resistance=3000 package=THT]  # not connected
  R11 = Resistor [tolerance=±5% power=0.25W resistance=3000 package=THT]  # not connected
  R12 = PHOTOCELL [package=photocell]  # not connected
  R13 = PHOTOCELL [package=photocell]  # not connected

nets:
  N1: Composant1.A0, R2.P$2, R6.Pin_0
  N2: Composant1.A1, R1.P$2, R5.Pin_0
  N3: Composant1.D3_PWM, R8.Pin_0, R9.Pin_1
  N4: Raspberry_Pi_1.GND, LED1.cathode, LED2.cathode
  N5: Raspberry_Pi_1.GIPO17, R7.Pin_1
  N6: R1.P$1, R2.P$1, R5.Pin_1, R6.Pin_1
  N7: R8.Pin_1, LED1.anode
  N8: LED2.anode, R9.Pin_0
